# Fritzing sketch Untitled Sketch (saved by Fritzing 0.9.3b)
breadboards: 1

parts:
  U1 = NodeMCU V1.0
  DHT11 = DHT11 basic temperature-humidity sensor [form="♂ (male)" package=THT]
  LCD_16x2_+_Module_I2C = LCD1602-I2C
  R1 = Resistor [tolerance=±5% resistance=220 package=THT]
  Fan = Fan - Ventilador [package=THT]
  MQ135 = MQ135 Hava Kalite Sensörü
  PIR_HC-SR501 = HC-SR501 [form="♀ (female)" package=THT]
  Module_Relay = 1 chan 5v relay module
  LED4 = LED - 5mm [color="White (4500K)" package="5 mm [THT]"]
  R3 = Resistor [tolerance=±5% resistance=220 package=THT]
  Module_LDR = LDR light sensor [package=THT]
  Power_plug1 = Power plug
  Buzzer = Buzzer 12mm [package=buzzer-12mm-ns]
  LED5 = LED - 5mm [color="Red (633nm)" package="5 mm [THT]"]

nets:
  N1: U1.D0, Module_Relay.pin_3
  N2: U1.D1, LCD_16x2_+_Module_I2C.SCL
  N3: U1.D3, DHT11.OUT
  N4: U1.D4, R3.Pin_1
  3V3: U1.3V3, DHT11.VCC, Module_LDR.pin3
  GND: U1.GND, DHT11.GND, LCD_16x2_+_Module_I2C.GND, Fan.GND, MQ135.GND, PIR_HC-SR501.GND, Module_Relay.pin_2, LED4.cathode, Module_LDR.pin2, Power_plug1.GND, Buzzer.2, LED5.cathode
  N5: U1.D5, Module_LDR.pin1
  N6: U1.D6, PIR_HC-SR501.SIG
  N7: U1.D7, R1.Pin_1
  N8: U1.D8, Buzzer.1
  N9: U1.A0, MQ135.A0
  VCC: LCD_16x2_+_Module_I2C.VCC, MQ135.VCC, MQ135.D0, PIR_HC-SR501.VCC, Module_Relay.pin_1, Module_Relay.pin_6, Power_plug1.VCC
  N10: R1.Pin_0, LED5.anode
  N11: Fan.5V, Module_Relay.pin_5
  N12: LED4.anode, R3.Pin_0

custom parts:
  NodeMCU V1.0: ESP8266 based NodeMCU
  DHT11 basic temperature-humidity sensor: The DHT11 is a basic, ultra low-cost digital temperature and humidity sensor. It uses a capacitive humidity sensor and a thermistor to measure the surrounding air, and spits out a digital signal on the data pin (no analog input pins needed). Its fairly simple to use, but requires careful timing to grab data. The only real downside of this sensor is you can only get new data from it once every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
  LCD1602-I2C: A standard character display, usually with 2x16 characters. Comes in many colors with LCM1602 IIC attached.
  Fan - Ventilador: Ventilador de 2 pines, se encuentra comunmente en computadoras de escritorio
  1 chan 5v relay module: 1 Channel 5V Relay Module Board Shield with Optocoupler Support High and Low Level Trigger for Arduino.
  LDR light sensor: Light sensor module. 3.3 V to 5V power.
  Buzzer 12mm: Buzzer 12mm Spark Fun Electronics SKU : Comp-Buzzer Through hole

// code stored in the sketch: Untitled.ino
#include <Arduino.h>
#include <DHT.h>
#include <Wire.h>
#include <LiquidCrystal_I2C.h>
#include <ESP8266WiFi.h>
#include <ESP8266WebServer.h>
#include <ESP8266HTTPClient.h>
#include <WiFiClientSecure.h>


// =====================================================
// 0. C?U HÌNH WIFI & GOOGLE SCRIPT WEBHOOK
// =====================================================
const char* WIFI_SSID     = "Phat";  
const char* WIFI_PASSWORD = "iloveiot102";    


const char* AP_SSID       = "SmartClassroom_WiFi";
const char* AP_PASS       = "12345678";


// Dán ???ng d?n Web App URL c?a Google Apps Script vào ?ây:
const char* GOOGLE_SCRIPT_URL = "https://script.google.com/macros/s/AKfycbwqhls0hb2drMwGw814XrDK-JxXPHil40b2adFl8XtYK-oC5IMo5byE8DOU8kQ2yy-4eQ/exec";


// Bi?n ch?ng spam mail (Ch? g?i 1 mail, sau 5 phút m?i ???c g?i ti?p n?u s? c? v?n còn)
unsigned long lastEmailSendTime = 0;
const unsigned long EMAIL_COOLDOWN = 300000; // 300.000 ms = 5 phút


// THÊM: 2 bi?n c? ?? ghi nh? s? ki?n ?ã g?i (Ph?c v? Logic Leo Thang)
bool tempEmailSent = false;
bool gasEmailSent = false;


ESP8266WebServer server(80);
String localIpStr = "Offline";


uint8_t fanMode   = 0; 
uint8_t lightMode = 0;


// =====================================================
// 1. KHAI BÁO CHÂN ESP8266
// =====================================================
#define PIR_PIN         14  // D5 - GPIO14
#define LDR_DO_PIN      12  // D6 - GPIO12
#define DHT_PIN          0  // D3 - GPIO0
#define MQ135_AO_PIN    A0  // A0 - MQ135 Analog Output


#define RELAY_FAN_PIN   16  // D0 - GPIO16
#define RELAY_LIGHT_PIN  2  // D4 - GPIO2
#define WARNING_LED_PIN 13  // D7 - GPIO13
#define BUZZER_PIN      15  // D8 - GPIO15


#define LCD_SDA_PIN      4  // D2 - GPIO4
#define LCD_SCL_PIN      5  // D1 - GPIO5
#define LCD_ADDR      0x27


// =====================================================
// 2. C?U HÌNH TH?I GIAN
// =====================================================
const unsigned long PIR_HOLD_TIME        = 15000;
const unsigned long PRINT_INTERVAL       = 1000;
const unsigned long SENSOR_INTERVAL      = 2000;
const unsigned long LCD_INTERVAL         = 2000;
const unsigned long ALARM_BLINK_INTERVAL = 300;


// =====================================================
// 3. DHT11 + LCD
// =====================================================
#define DHTTYPE DHT11
DHT dht(DHT_PIN, DHTTYPE);
LiquidCrystal_I2C lcd(LCD_ADDR, 16, 2);


// =====================================================
// 4. C?U HÌNH RELAY / ?ÈN & NG??NG DEMO
// =====================================================
#define FAN_ACTIVE_HIGH  true
#define LIGHT_ACTIVE_LOW false


#define TEMP_FAN_ON      35.0f
#define TEMP_FAN_OFF     34.5f
#define TEMP_ALARM_ON    35.0f
#define TEMP_ALARM_OFF   34.5f


#define MQ135_ALARM_ON   500
#define MQ135_ALARM_OFF  450


// =====================================================
// 5. BI?N TR?NG THÁI
// =====================================================
volatile bool pirInterruptTriggered = false;
bool motionDetected = false;
unsigned long lastMotionTime = 0;


float currentTemp = NAN;
float currentHum = NAN;
bool dhtError = true;
int mq135Raw = 0;
bool isDark = false;


bool tempFanNeed = false; 
bool fanOn = false;       
bool lightOn = false;


bool tempAlarm = false;
bool gasAlarm = false;
bool alarmActive = false;
bool blinkState = false;


unsigned long lastSensorReadMs = 0;
unsigned long lastPrintTime = 0;
unsigned long lastBlinkMs = 0;
unsigned long lastLcdUpdateMs = 0;


uint8_t lcdPage = 0;
uint8_t lcdResetCounter = 0;


void IRAM_ATTR onPirRisingEdge() {
  pirInterruptTriggered = true;
}


void setFanRelay(bool turnOn) {
  if (FAN_ACTIVE_HIGH) {
    digitalWrite(RELAY_FAN_PIN, turnOn ? HIGH : LOW);
  } else {
    digitalWrite(RELAY_FAN_PIN, turnOn ? LOW : HIGH);
  }
}


void setLightRelay(bool turnOn) {
  if (LIGHT_ACTIVE_LOW) {
    digitalWrite(RELAY_LIGHT_PIN, turnOn ? LOW : HIGH);
  } else {
    digitalWrite(RELAY_LIGHT_PIN, turnOn ? HIGH : LOW);
  }
}


void printLcdLine(uint8_t row, const char* text) {
  char buf[17];
  snprintf(buf, sizeof(buf), "%-16s", text);
  lcd.setCursor(0, row);
  lcd.print(buf);
}


// =====================================================
// 6. HÀM G?I EMAIL CHUYÊN NGHI?P T?I GOOGLE SCRIPT
// =====================================================
void sendAlertEmail(String temp, String gas) {
  if (WiFi.status() == WL_CONNECTED) {
    WiFiClientSecure client;
    client.setInsecure(); // B? qua ch?ng ch? SSL
    
    HTTPClient http;
    // URL thông minh: Ch? ghép nh?ng ch? s? th?c s? ?ang có s? c?
    String url = String(GOOGLE_SCRIPT_URL) + "?";
    
    if (temp != "") url += "temp=" + temp + "&";
    if (gas != "") url += "gas=" + gas;
    
    Serial.println(">>> ?ang g?i Webhook g?i Email HTML...");
    http.begin(client, url);
    
    // L?NH ÉP ?I THEO CHUY?N H??NG C?A GOOGLE (B?T BU?C)
    http.setFollowRedirects(HTTPC_STRICT_FOLLOW_REDIRECTS);
    
    int httpCode = http.GET();
    
    if (httpCode > 0) {
      Serial.println("==> HTTP Code: " + String(httpCode));
      if (httpCode == HTTP_CODE_OK || httpCode == 302) {
        Serial.println("==> G?I MAIL HTML THÀNH CÔNG!");
      }
    } else {
      Serial.println("==> L?i k?t n?i, mã l?i: " + http.errorToString(httpCode));
    }
    http.end();
  }
}


// =====================================================
// 7. WEB SERVER DASHBOARD
// =====================================================
void handleRoot() {
  String html = R"rawliteral(
<!DOCTYPE html><html><head><meta charset="UTF-8">
<meta name="viewport" content="width=device-width, initial-scale=1.0">
<title>Smart Classroom Dashboard</title>
<style>
  body{font-family:Arial,sans-serif;background:#f0f4f8;margin:0;padding:15px;text-align:center;color:#333;}
  h2{color:#1a73e8;margin-bottom:10px;}
  .status-bar{padding:12px;border-radius:8px;font-weight:bold;color:#fff;margin-bottom:15px;font-size:18px;}
  .safe{background:#28a745;} .danger{background:#dc3545;animation:blink 0.8s infinite;}
  @keyframes blink{50%{opacity:0.4;}}
  .grid{display:grid;grid-template-columns:repeat(auto-fit,minmax(145px,1fr));gap:12px;max-width:650px;margin:auto;}
  .card{background:#fff;padding:15px;border-radius:10px;box-shadow:0 2px 6px rgba(0,0,0,0.08);}
  .val{font-size:24px;font-weight:bold;color:#1a73e8;margin-top:6px;}
  .ctrl{max-width:650px;margin:15px auto;background:#fff;padding:15px;border-radius:10px;box-shadow:0 2px 6px rgba(0,0,0,0.08);}
  button{padding:8px 14px;margin:4px;border:none;border-radius:6px;font-weight:bold;cursor:pointer;color:#fff;}
  .btn-auto{background:#6c757d;} .btn-on{background:#28a745;} .btn-off{background:#dc3545;}
</style></head><body>
  <h2>SMART CLASSROOM IoT</h2>
  <div id="alarmBox" class="status-bar safe">HE THONG AN TOAN</div>
  <div class="grid">
    <div class="card">Nhi?t ??<div class="val" id="temp">-- °C</div></div>
    <div class="card">?? ?m<div class="val" id="hum">-- %</div></div>
    <div class="card">Khí Gas (MQ135)<div class="val" id="gas">--</div></div>
    <div class="card">Ánh sáng<div class="val" id="ldr">--</div></div>
    <div class="card">Chuy?n ??ng PIR<div class="val" id="pir">--</div></div>
    <div class="card">Thi?t b?<div class="val" style="font-size:16px" id="dev">--</div></div>
  </div>
  <div class="ctrl">
    <div><b>?i?u khi?n Qu?t:</b> (<span id="fMode">AUTO</span>)<br>
      <button class="btn-auto" onclick="setMode('fan',0)">AUTO</button>
      <button class="btn-on" onclick="setMode('fan',1)">B?T</button>
      <button class="btn-off" onclick="setMode('fan',2)">T?T</button>
    </div><hr style="border:0;border-top:1px solid #eee;margin:12px 0;">
    <div><b>?i?u khi?n ?èn h?c:</b> (<span id="lMode">AUTO</span>)<br>
      <button class="btn-auto" onclick="setMode('light',0)">AUTO</button>
      <button class="btn-on" onclick="setMode('light',1)">B?T</button>
      <button class="btn-off" onclick="setMode('light',2)">T?T</button>
    </div>
  </div>
<script>
  function setMode(dev,m){fetch('/control?dev='+dev+'&mode='+m).then(()=>loadData());}
  function loadData(){
    fetch('/data').then(r=>r.json()).then(d=>{
      document.getElementById('temp').innerText = d.dhtErr ? 'L?I!' : d.temp.toFixed(1)+' °C';
      document.getElementById('hum').innerText  = d.dhtErr ? '--' : d.hum.toFixed(0)+' %';
      document.getElementById('gas').innerText  = d.gas;
      document.getElementById('ldr').innerText  = d.dark ? 'T?I' : 'SÁNG';
      document.getElementById('pir').innerText  = d.pir ? 'CÓ NG??I' : 'V?NG';
      document.getElementById('dev').innerText  = 'Qu?t: '+(d.fan?'ON':'OFF')+' | ?èn: '+(d.light?'ON':'OFF');
      const mNames = ['AUTO','B?T TAY','T?T TAY'];
      document.getElementById('fMode').innerText = mNames[d.fMode];
      document.getElementById('lMode').innerText = mNames[d.lMode];
      const ab = document.getElementById('alarmBox');
      if(d.gasAlarm){ab.className='status-bar danger';ab.innerText='! C?NH BÁO RÒ R? KHÍ GAS !';}
      else if(d.tempAlarm){ab.className='status-bar danger';ab.innerText='! C?NH BÁO NHI?T ?? CAO !';}
      else{ab.className='status-bar safe';ab.innerText='H? TH?NG BÌNH TH??NG';}
    });
  }
  setInterval(loadData, 1500); loadData();
</script></body></html>
)rawliteral";
  server.send(200, "text/html", html);
}


void handleData() {
  String json = "{";
  json += "\"temp\":" + String(isnan(currentTemp) ? 0 : currentTemp, 1) + ",";
  json += "\"hum\":" + String(isnan(currentHum) ? 0 : currentHum, 0) + ",";
  json += "\"dhtErr\":" + String(dhtError ? "true" : "false") + ",";
  json += "\"gas\":" + String(mq135Raw) + ",";
  json += "\"dark\":" + String(isDark ? "true" : "false") + ",";
  json += "\"pir\":" + String(motionDetected ? "true" : "false") + ",";
  json += "\"fan\":" + String(fanOn ? "true" : "false") + ",";
  json += "\"light\":" + String(lightOn ? "true" : "false") + ",";
  json += "\"fMode\":" + String(fanMode) + ",";
  json += "\"lMode\":" + String(lightMode) + ",";
  json += "\"gasAlarm\":" + String(gasAlarm ? "true" : "false") + ",";
  json += "\"tempAlarm\":" + String(tempAlarm ? "true" : "false");
  json += "}";
  server.send(200, "application/json", json);
}


void handleControl() {
  if (server.hasArg("dev") && server.hasArg("mode")) {
    String dev = server.arg("dev");
    uint8_t m = server.arg("mode").toInt();
    if (m <= 2) {
      if (dev == "fan") fanMode = m;
      else if (dev == "light") lightMode = m;
    }
  }
  server.send(200, "text/plain", "OK");
}


// =====================================================
// 8. SETUP
// =====================================================
void setup() {
  Serial.begin(115200);
  delay(500);


  pinMode(PIR_PIN, INPUT);
  pinMode(LDR_DO_PIN, INPUT);
  pinMode(RELAY_FAN_PIN, OUTPUT);
  pinMode(RELAY_LIGHT_PIN, OUTPUT);
  pinMode(WARNING_LED_PIN, OUTPUT);
  pinMode(BUZZER_PIN, OUTPUT);


  attachInterrupt(digitalPinToInterrupt(PIR_PIN), onPirRisingEdge, RISING);


  Wire.begin(LCD_SDA_PIN, LCD_SCL_PIN);
  Wire.setClock(50000);
  delay(100);
  lcd.init();
  lcd.backlight();
  printLcdLine(0, "Smart Classroom");
  printLcdLine(1, "Testing H/W...");


  // Test ph?n c?ng 1 giây
  setFanRelay(true);
  setLightRelay(true);
  digitalWrite(WARNING_LED_PIN, HIGH);
  digitalWrite(BUZZER_PIN, HIGH);
  delay(1000);


  setFanRelay(false);
  setLightRelay(false);
  digitalWrite(WARNING_LED_PIN, LOW);
  digitalWrite(BUZZER_PIN, LOW);


  // K?t n?i WiFi (T?i ?a 15 giây ?? ch?ng l?i Hotspot)
  delay(100);
  lcd.init();
  lcd.backlight();
  printLcdLine(0, "Connecting WiFi");
  printLcdLine(1, WIFI_SSID);


  WiFi.mode(WIFI_STA);
  WiFi.disconnect();
  delay(100);
  WiFi.begin(WIFI_SSID, WIFI_PASSWORD);
  unsigned long startWifiMs = millis();
  while (WiFi.status() != WL_CONNECTED && (millis() - startWifiMs < 15000)) {
    delay(400);
  }


  if (WiFi.status() == WL_CONNECTED) {
    localIpStr = WiFi.localIP().toString();
    printLcdLine(0, "WiFi Connected!");
    printLcdLine(1, localIpStr.c_str());
  } else {
    WiFi.mode(WIFI_AP);
    WiFi.softAP(AP_SSID, AP_PASS);
    localIpStr = WiFi.softAPIP().toString();
    printLcdLine(0, "AP Mode Active");
    printLcdLine(1, localIpStr.c_str());
  }


  server.on("/", handleRoot);
  server.on("/data", handleData);
  server.on("/control", handleControl);
  server.begin();


  dht.begin();
  delay(2500);
}


// =====================================================
// 9. LOOP
// =====================================================
void loop() {
  unsigned long currentTime = millis();
  server.handleClient();


  // 1. X? LÝ PIR
  bool currentPirHigh = (digitalRead(PIR_PIN) == HIGH);
  if (pirInterruptTriggered || currentPirHigh) {
    motionDetected = true;
    lastMotionTime = currentTime;
    pirInterruptTriggered = false;
  }
  if (motionDetected && (currentTime - lastMotionTime >= PIR_HOLD_TIME)) {
    motionDetected = false;
  }


  // 2. ??C LDR & ?I?U KHI?N ?ÈN H?C
  isDark = (digitalRead(LDR_DO_PIN) == HIGH);
  if (lightMode == 0) lightOn = (isDark && motionDetected);
  else if (lightMode == 1) lightOn = true;
  else lightOn = false;
  setLightRelay(lightOn);


  // 3. ??C DHT11 + MQ135 (M?i 2 giây)
  if (currentTime - lastSensorReadMs >= SENSOR_INTERVAL) {
    lastSensorReadMs = currentTime;


    // --- 3.1 ??c MQ135 ---
    mq135Raw = analogRead(MQ135_AO_PIN);
    if (mq135Raw >= MQ135_ALARM_ON) {
      gasAlarm = true;
    } else if (mq135Raw <= MQ135_ALARM_OFF) {
      gasAlarm = false;
    }


    // --- 3.2 ??c DHT11 ---
    float t = dht.readTemperature();
    float h = dht.readHumidity();


    if (isnan(t) || isnan(h)) {
      dhtError = true;
      tempFanNeed = false;
      tempAlarm = false;
    } else {
      dhtError = false;
      currentTemp = t;
      currentHum = h;


      if (currentTemp >= TEMP_FAN_ON) {
        tempFanNeed = true;
      } else if (currentTemp <= TEMP_FAN_OFF) {
        tempFanNeed = false;
      }


      if (currentTemp >= TEMP_ALARM_ON) {
        tempAlarm = true;
      } else if (currentTemp <= TEMP_ALARM_OFF) {
        tempAlarm = false;
      }
    }


    // T?ng h?p ?i?u khi?n Qu?t
    if (gasAlarm) {
      fanOn = true;
    } else if (fanMode == 0) {
      fanOn = tempFanNeed;
    } else if (fanMode == 1) {
      fanOn = true;
    } else {
      fanOn = false;
    }
    setFanRelay(fanOn);


    // T?ng h?p c?nh báo
    alarmActive = (gasAlarm || tempAlarm);
    
    // --- 3.3 THU?T TOÁN G?I EMAIL LEO THANG (ESCALATION ALERT) ---
    bool needToSendEmail = false;


    // Ki?m tra xem có s? c? M?I nào v?a xu?t hi?n mà ch?a báo cáo không?
    if (gasAlarm && !gasEmailSent) {
      needToSendEmail = true; // Xé rào n?u có Khí Gas rò r? m?i
    }
    if (tempAlarm && !tempEmailSent) {
      needToSendEmail = true; // Xé rào n?u có Nhi?t ?? cao m?i
    }


    // Ki?m tra xem ?ã h?t 5 phút ?? g?i mail nh?c nh? ch?a?
    if (alarmActive && lastEmailSendTime != 0 && (currentTime - lastEmailSendTime >= EMAIL_COOLDOWN)) {
      needToSendEmail = true; 
    }


    // Th?c hi?n g?i mail
    if (needToSendEmail) {
      lastEmailSendTime = currentTime; 
      tempEmailSent = tempAlarm;       // Ghi nh? l?i tr?ng thái ?ã báo cáo     
      gasEmailSent = gasAlarm;         
      
      String tempToPush = "";
      String gasToPush = "";


      // Ch? ?óng gói d? li?u c?a s? ki?n ?ang v??t ng??ng
      if (tempAlarm) {
        tempToPush = String(currentTemp, 1);
      }
      if (gasAlarm) {
        gasToPush = String(mq135Raw);
      }
      
      // G?i hàm g?i Email
      sendAlertEmail(tempToPush, gasToPush);
    }


    // Khi an toàn, Reset b? nh? (Ch? reset sau 5 phút ?? tránh ch?p ch?n)
    if (!alarmActive) {
      if (currentTime - lastEmailSendTime >= EMAIL_COOLDOWN) {
        lastEmailSendTime = 0; 
        tempEmailSent = false;
        gasEmailSent = false;
      }
    }


    if (!alarmActive) {
      blinkState = false;
      digitalWrite(WARNING_LED_PIN, LOW);
      digitalWrite(BUZZER_PIN, LOW);
    }
  }


  // 4. HI?N TH? LCD (M?i 2 giây)
  if (currentTime - lastLcdUpdateMs >= LCD_INTERVAL) {
    lastLcdUpdateMs = currentTime;


    lcdResetCounter++;
    if (lcdResetCounter >= 10) {
      lcdResetCounter = 0;
      lcd.init();
      lcd.backlight();
    }


    char line0[17];
    char line1[17];


    if (gasAlarm) {
      snprintf(line0, sizeof(line0), "! CANH BAO KHI !");
      snprintf(line1, sizeof(line1), "Gas:%d Fan:ON", mq135Raw);
    } else if (tempAlarm) {
      snprintf(line0, sizeof(line0), "! NHIET DO CAO !");
      snprintf(line1, sizeof(line1), "T:%.1fC Fan:ON", currentTemp);
    } else {
      if (lcdPage == 0) {
        if (dhtError) {
          snprintf(line0, sizeof(line0), "DHT: LOI DOC!");
        } else {
          snprintf(line0, sizeof(line0), "T:%.1fC H:%.0f%%", currentTemp, currentHum);
        }
        snprintf(line1, sizeof(line1), "Gas:%d %s", mq135Raw, isDark ? "TOI" : "SANG");
      } else {
        snprintf(line0, sizeof(line0), "PIR:%s", motionDetected ? "CO NGUOI" : "VANG");
        snprintf(line1, sizeof(line1), "Fan:%s Den:%s", fanOn ? "ON " : "OFF", lightOn ? "ON" : "OFF");
      }
      lcdPage = (lcdPage + 1) % 2;
    }


    printLcdLine(0, line0);
    printLcdLine(1, line1);
  }


  // 5. IN RA SERIAL MONITOR (M?i 1 giây)
  if (currentTime - lastPrintTime >= PRINT_INTERVAL) {
    lastPrintTime = currentTime;


    Serial.printf("[IP: %s] PIR:%-5s | LDR:%-4s | MQ135:%-4d | ",
                  localIpStr.c_str(),
                  motionDetected ? "CO" : "KHONG",
                  isDark ? "TOI" : "SANG",
                  mq135Raw);


    if (dhtError) {
      Serial.print("DHT:LOI! | ");
    } else {
      Serial.printf("T:%.1f*C H:%.0f%% | ", currentTemp, currentHum);
    }


    Serial.printf("Quat:%-3s | Den:%-3s | %s\n",
                  fanOn ? "BAT" : "TAT",
                  lightOn ? "BAT" : "TAT",
                  gasAlarm ? "CANH BAO KHI GAS!" : (tempAlarm ? "NHIET DO CAO!" : "An toan"));
  }


  // 6. NH?P NHÁY ?ÈN & CÒI (CH? HÚ KHI CÓ GAS)
  if (alarmActive) {
    if (currentTime - lastBlinkMs >= ALARM_BLINK_INTERVAL) {
      lastBlinkMs = currentTime;
      blinkState = !blinkState;
      
      // ?èn luôn ch?p báo hi?u có s? ki?n
      digitalWrite(WARNING_LED_PIN, blinkState ? HIGH : LOW);
      
      // Còi ch? kích ho?t n?u có rò r? khí Gas
      if (gasAlarm) {
        digitalWrite(BUZZER_PIN, blinkState ? HIGH : LOW);
      } else {
        digitalWrite(BUZZER_PIN, LOW); // Ép t?t còi n?u ch? là báo nhi?t ??
      }
    }
  }
}
